# Fritzing sketch wiring (saved by Fritzing 0.9.4)

parts:
  Part2 = Altitude/Pressure Sensor - MPL3115A2 Breakout [part_number=SEN-11084]
  U1 = ESP32-38PinWide [part_number=ESP32-38PinWide]
  Part4 = Adafruit Si7021 Temp Humidity [part_number="Adafruit #3251"]

nets:
  N1: Part2.SDA, U1.GPIO21, Part4.SDA
  N2: Part2.SCL, U1.GPIO22, Part4.SCL
  VCC: Part2.VCC, U1.3.3, Part4.+3V3
  GND: Part2.GND, U1.GND, Part4.GND

custom parts:
  ESP32-38PinWide: Generic 38-Pin ESP32 with wide format (only access to one side of pins on a breadboard) based on Stephen Lilley's HiLetgo ESP-WROOM-32 ESP32 ESP-32S Development Board.
  Adafruit Si7021 Temp Humidity: It's summer and you're sweating and your hair's all frizzy and all you really want to know is why the weatherman said this morning that today's relative humidity would max out at a perfectly reasonable 42% when it feels more like 77%. Enter the Si7021 Temperature + Humidity Sensor - the best way to prove the weatherman wrong! This lovely sensor for Silicon labs has ± 3% relative humidity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
